# Fritzing sketch detai3_nhom3 (saved by Fritzing 1.0.2b)

parts:
  R2 = Resistor [tolerance=±5% resistance=220 power=0.25W package=THT]
  Keypad4x1 = Keypad Membran 4x4
  Part1 = Arduino Uno (Rev3)
  LED1 = RGB LED (com. cathode, rgb) [color="Red (633nm)" current=0.030A package="5 mm [THT]"]
  R11 = 12mm Trimmer Potentiometer (Large) [maximum_resistance=10kΩ knob_status=50% power=0.5W package=THT]
  J2 = Basic Servo
  LCD1 = LCD screen
  R12 = Resistor [tolerance=±5% resistance=220 power=0.25W package=THT]
  R13 = Resistor [tolerance=±5% resistance=220 power=0.25W package=THT]

nets:
  N1: R2.Pin_0, LED1.common_cathode
  GND: R2.Pin_1, Part1.GND, R11.leg2, J2.gnd, R12.Pin_0, R13.Pin_0
  N2: Keypad4x1.Pin1, Part1.D9_PWM
  N3: Keypad4x1.Pin2, Part1.D8
  N4: Keypad4x1.Pin3, Part1.D7
  N5: Keypad4x1.Pin4, Part1.D6_PWM
  N6: Keypad4x1.Pin5, Part1.D5_PWM
  N7: Keypad4x1.Pin6, Part1.D4
  N8: Keypad4x1.Pin7, Part1.D3_PWM
  N9: Keypad4x1.Pin8, Part1.D2
  N10: Part1.A0, LCD1.RS
  N11: Part1.A1, LCD1.E
  N12: Part1.A2, LCD1.DB4
  N13: Part1.A3, LCD1.DB5
  N14: Part1.A4/SDA, LCD1.DB6
  N15: Part1.A5/SCL, LCD1.DB7
  N16: Part1.D10_PWM/SS, J2.pulse
  N17: Part1.D11_PWM/MOSI, LED1.green_anode
  N18: Part1.D12/MISO, LED1.blue_anode
  N19: Part1.D13/SCK, LED1.red_anode
  5V: Part1.5V, R11.leg1, J2.vcc, LCD1.LED+
  N20: R11.wiper, LCD1.V0
  VSS: LCD1.VSS, LCD1.VDD, LCD1.R/W, LCD1.DB0, LCD1.DB1, LCD1.DB2, LCD1.DB3, R13.Pin_1
  N21: LCD1.LED-, R12.Pin_1

custom parts:
  Keypad Membran 4x4: Membrane Keypad 4x4 Matrix

// code stored in the sketch: Code_detai3_nhom3.ino
#include <Keypad.h>
#include <Servo.h>
#include <LiquidCrystal.h>

#define red 13
#define green 11
#define blue 12

#define servo 10

LiquidCrystal lcd(A0, A1, A2, A3, A4, A5);

Servo servo1;

const byte rows = 4;
const byte cols = 4;
char keys[rows][cols] = {
  {'1', '2', '3', 'A'},
  {'4', '5', '6', 'B'},
  {'7', '8', '9', 'C'},
  {'*', '0', '#', 'D'}
};

byte row[rows] = {9,8,7,6};
byte col[cols] = {5,4,3,2};

Keypad keypad = Keypad(makeKeymap(keys), row, col, rows, cols);

String pass = "";
bool isASetPass = false;
int trangthai = 0;

void setup() {
  Serial.begin(9600);  
  lcd.begin(16, 2);
  
  pinMode(red, OUTPUT);
  pinMode(green, OUTPUT);
  pinMode(blue, OUTPUT);

  servo1.attach(servo);
   analogWrite(red, 0);
  analogWrite(green, 0);
  analogWrite(blue, 0);
  lcd.print("No Password");
}

void loop() {
  char key = keypad.getKey();
  
  if (key) {
    if (!isASetPass && key == 'A') {
      lcd.clear();
      lcd.print("Dat mat khau:");
      setpass();
    }
    else if (isASetPass && key == 'B') {
      lcd.clear();
      lcd.print("Nhap mat khau:");
      checkpass();
    }
    else if (trangthai == 3 && key == 'C') {
      lock();
    }
  }
}

void setpass() {
  Serial.println("Nhap mat khau lan 1:");
  while (!Serial.available()) {}
  String p1 = Serial.readStringUntil('\n');
  lcd.clear();
  lcd.print(p1);
  
  Serial.println("Nhap lai mat khau:");
  while (!Serial.available()) {}
  String p2 = Serial.readStringUntil('\n');
  lcd.clear();
  lcd.print(p2); 
  
  if (p1 == p2) {
    pass = p1;
    isASetPass = true;
    lock();
  } else {
    lcd.clear();
    lcd.print("Khong khop!");
    delay(2000);
    lcd.clear();
    lcd.print("Khong co mat khau");
  }
}

void checkpass() {
  int i = 3;
  
  while (i--) {
    Serial.println("Nhap mat khau:");
    while (!Serial.available()) {}
    String input = Serial.readStringUntil('\n');
    lcd.clear();
    lcd.print(input);
    delay(1000);
    
    if (input == pass) {
      unlock();
      return;
    } else {
      lcd.clear();
      lcd.print("Sai! Con ");
      lcd.print(i);
      lcd.print(" lan");
      delay(500);
    }
  }
  
  canhbao();
}

void lock() {
  trangthai = 1;
  servo1.write(90);
   analogWrite(red, 255);
  analogWrite(green, 255);
  analogWrite(blue, 255);
  lcd.clear();
  lcd.print("Da khoa");
}

void unlock() {
  trangthai = 2;
  servo1.write(180);
   analogWrite(red, 0);
  analogWrite(green, 255);
  analogWrite(blue, 0);
  lcd.clear();
  lcd.print("Da mo khoa");
  delay(10000);
  lock();
}

void canhbao() {
  trangthai = 3;
  analogWrite(red, 255);
  analogWrite(green, 0);
  analogWrite(blue, 0);
  lcd.clear();
  lcd.print("CANH BAO!!!");
}
